# Fritzing sketch Wiring_Schematic (saved by Fritzing 0.9.3b)
breadboards: 1

parts:
  Transmitter_Uno1 = Arduino Uno (Rev3)
  Heltec_CubeCell_Dev-Board2 = Heltec CubeCell Dev-Board [part_number=HTCC-AB01]
  External_LM35 = LM34 Temperature Sensor [package="TO92 [THT]"]
  VCC_(6V)1 = 4 x AAA Battery Mount
  Internal_LM35 = LM34 Temperature Sensor [package="TO92 [THT]"]

nets:
  N1: Transmitter_Uno1.A2, Internal_LM35.Vout
  N2: Transmitter_Uno1.A3, External_LM35.Vout
  N3: Transmitter_Uno1.D0/RX, Heltec_CubeCell_Dev-Board2.pin6
  N4: Transmitter_Uno1.D1/TX, Heltec_CubeCell_Dev-Board2.pin5
  N5: Transmitter_Uno1.3V3, Heltec_CubeCell_Dev-Board2.pin_10
  N6: Transmitter_Uno1.5V, External_LM35.+Vs, Internal_LM35.+Vs
  GND: Transmitter_Uno1.GND, Heltec_CubeCell_Dev-Board2.pin_11, Heltec_CubeCell_Dev-Board2.pin_14, Heltec_CubeCell_Dev-Board2.pin_18, External_LM35.GND, VCC_(6V)1.-, Internal_LM35.GND
  N7: Transmitter_Uno1.VIN, VCC_(6V)1.+

custom parts:
  Heltec CubeCell Dev-Board: CubeCell is a part of the Heltec LoRa series and incorporates an ASR6501 processor and SX1262 RF transceiver with an integrated CP2102 USB to serial port interface and onboard SHT1.25 battery interface with integrated lithium battery management system supporting direct solar panel connection.
